// Digital circuit main.dig as structural Verilog
module main (
  input  clk
);

  wire C, P_out, S_out;
  wire [15:0] Exceptions;
  wire [31:0] pc_1_pc;

  PC pc_1 (.C(C), .PC(pc_1_pc));
  Memory memory_1 (
    .Addr({32{1'b0}}), .D_in({32{1'b0}}), .PC(pc_1_pc), .C(C), .str(1'b0), .ld(1'b0), .Except(Exceptions));  // open: D_out, Instr
  LED Store_AMO_Page_Fault (.in(Exceptions[15]));
  LED led_1 (.in(Exceptions[14]));
  LED Load_Page_Fault (.in(Exceptions[13]));
  LED Instruction_Page_Fault (.in(Exceptions[12]));
  LED Environment_Call_From_M_mode (.in(Exceptions[11]));
  LED led_2 (.in(Exceptions[10]));
  LED Environment_Call_From_S_mode (.in(Exceptions[9]));
  LED Environment_Call_From_U_mode (.in(Exceptions[8]));
  LED Store_AMO_Access_Fault (.in(Exceptions[7]));
  LED Store_AMO_Address_Misaligned (.in(Exceptions[6]));
  LED Load_Access_Fault (.in(Exceptions[5]));
  LED Load_Address_Misaligned (.in(Exceptions[4]));
  LED Breakpoint (.in(Exceptions[3]));
  LED Illegal_Instruction (.in(Exceptions[2]));
  LED Instruction_Access_Fault (.in(Exceptions[1]));
  LED Instruction_Address_Misaligned (.in(Exceptions[0]));
  Clock #(.generic("Scale := 50;")) clock_1 (.C_in(clk), .Start_Stop(P_out), .Step(S_out), .C(C));
  Button P (.out(P_out));
  Button S (.out(S_out));

  // Notes on the sheet:
  //   clk: Hz: 50
endmodule
